# Fritzing sketch SSPMeteo2-ESQUEMA (saved by Fritzing 0.9.3b)
circuit board: 3.50866cm x 5.31575cm

parts:
  R = Resistor [tolerance=±5% resistance=10k package=THT]
  Veleta = Basic Force Sensing Resistor (FSR) [package=THT]
  DHT22 = Humidity and Temperature Sensor RHT03
  U1 = BMP085 Pressure Sensor [package=bmp085]
  Lluvia = Reed switch [package=THT]
  Anemometro = Reed switch [package=THT]
  WeMos_D1_R2 = WeMos D1 Mini
  J3 = Camdenboss CTB0158-5 [part_number=CTB0158-5 package=THT]
  J4 = Camdenboss CTB0158-5 [part_number=CTB0158-5 package=THT]
  J6 = Camdenboss CTB0158-2 [part_number=CTB0158-2 package=THT]
  J7 = Camdenboss CTB0158-3 [part_number=CTB0158-3 package=THT]
  Componente1 = BME280 Breakout  # not connected

nets:
  N1: R.Pin_0, WeMos_D1_R2.3V3, J7.pin1, J7.pin2, J7.pin3
  N2: R.Pin_1, WeMos_D1_R2.A0, J4.pin4
  N3: Veleta.pin_0, J3.terminal_5
  N4: Veleta.pin_1, J4.terminal_4
  N5: DHT22.Vcc, J7.terminal_3
  N6: DHT22.Data-signal, J4.terminal_3
  N7: DHT22.GND_2, J3.terminal_4
  N8: U1.GND, J3.terminal_3
  N9: U1.VDDA, J7.terminal_2
  N10: U1.SCL, J6.terminal_1
  N11: U1.SDA, J4.terminal_5
  N12: Lluvia.pin_1, J3.terminal_2
  N13: Lluvia.pin_2, J4.terminal_1
  N14: Anemometro.pin_1, J3.terminal_1
  N15: Anemometro.pin_2, J4.terminal_2
  N16: WeMos_D1_R2.D1, J6.pin1
  N17: WeMos_D1_R2.D2, J4.pin5
  N18: WeMos_D1_R2.D3, J4.pin1
  N19: WeMos_D1_R2.D5, J4.pin3
  N20: WeMos_D1_R2.D6, J4.pin2
  N21: WeMos_D1_R2.G, J3.pin1, J3.pin2, J3.pin3, J3.pin4, J3.pin5

notes:
  SSPMeteo
  T/H
  R
  5V
  GND
  WD
  WS
  DATA
  VCC
  RF433
  sensores
  SSPMeteo2, Estacion meteorologica, 1.0
  Anemometro y lluvia usan resistencias pullup internas.
  NO VALIDO
